// Logisim project Zadanie0-tutorial.circ as structural Verilog: 1 circuit, main circuit main
module main (
  input  \wejście_x ,
  input  \wejście_y ,
  output \wyjście 
);

  wire and_1_out, and_2_out, not_1_out, not_2_out;

  not not_1 (not_1_out, \wejście_x );
  not not_2 (not_2_out, \wejście_y );
  and and_1 (and_1_out, not_1_out, \wejście_y );
  and and_2 (and_2_out, \wejście_x , not_2_out);
  or or_1 (\wyjście , and_1_out, and_2_out);
endmodule
