// Logisim project 74194 — kopia.circ as structural Verilog: 6 circuits, main circuit main
module main (
  input  B,
  input  C,
  input  D,
  input  A,
  input  S1,
  input  S0,
  input  SL___LIN,
  input  SR___RIN,
  input  CLK,
  input  CLR,
  output QA,
  output QB,
  output QC,
  output QD
);

  wire and_1_out, and_2_out, and_3_out, and_4_out, and_5_out, and_6_out, and_7_out, and_8_out, and_9_out,
       and_10_out, and_11_out, and_12_out, and_13_out, and_14_out, and_15_out, and_16_out, nor_1_out,
       nor_2_out, nor_3_out, nor_4_out, not_1_out, not_2_out, not_3_out, not_4_out, not_5_out, not_6_out,
       not_7_out, or_1_out;

  not not_1 (not_1_out, S1);
  not not_2 (not_2_out, S0);
  and and_1 (and_1_out, SR___RIN, not_1_out, S0);
  and and_2 (and_2_out, S0, S1, A);
  nor nor_1 (nor_1_out, and_1_out, and_2_out, and_4_out, and_3_out);
  not not_3 (not_3_out, CLR);
  or or_1 (or_1_out, not_3_out, CLR);
  and and_3 (and_3_out, not_2_out, not_1_out, QA);
  and and_4 (and_4_out, not_2_out, S1, QB);
  S_R_Flip_Flop s_r_ff_1 (
    .S(not_4_out), .clk(CLK), .R(nor_1_out), .Q(QA), .reset(CLR), .en(or_1_out));  // open: Qn, preset
  not not_4 (not_4_out, nor_1_out);
  and and_5 (and_5_out, QA, not_1_out, S0);
  and and_6 (and_6_out, S0, S1, B);
  and and_7 (and_7_out, not_2_out, S1, QC);
  nor nor_2 (nor_2_out, and_5_out, and_6_out, and_7_out, and_8_out);
  not not_5 (not_5_out, nor_2_out);
  and and_8 (and_8_out, not_2_out, not_1_out, QB);
  S_R_Flip_Flop s_r_ff_2 (
    .S(not_5_out), .clk(CLK), .R(nor_2_out), .Q(QB), .reset(CLR), .en(or_1_out));  // open: Qn, preset
  and and_9 (and_9_out, QB, not_1_out, S0);
  and and_10 (and_10_out, S0, S1, C);
  nor nor_3 (nor_3_out, and_9_out, and_10_out, and_11_out, and_12_out);
  and and_11 (and_11_out, not_2_out, S1, QD);
  and and_12 (and_12_out, not_2_out, not_1_out, QC);
  S_R_Flip_Flop s_r_ff_3 (
    .S(not_6_out), .clk(CLK), .R(nor_3_out), .Q(QC), .reset(CLR), .en(or_1_out));  // open: Qn, preset
  not not_6 (not_6_out, nor_3_out);
  and and_13 (and_13_out, S0, S1, D);
  and and_14 (and_14_out, QC, not_1_out, S0);
  and and_15 (and_15_out, not_2_out, S1, SL___LIN);
  nor nor_4 (nor_4_out, and_14_out, and_13_out, and_15_out, and_16_out);
  not not_7 (not_7_out, nor_4_out);
  and and_16 (and_16_out, not_2_out, not_1_out, QD);
  S_R_Flip_Flop s_r_ff_4 (
    .S(not_7_out), .clk(CLK), .R(nor_4_out), .Q(QD), .reset(CLR), .en(or_1_out));  // open: Qn, preset

  // Notes on the sheet:
  //   eduinf.waw.pl/inf/prg/010_uc/74194.php
  //   Sygnał Enable - zawsze aktywny
  //   schemat według dokumentacji: www.ti.com/lit/ds/symlink/sn74ls194a.pdf
  //   wersja 2, traktuje symbole O jako podłączenia z NOT
endmodule

module Uproszczony (
  input  S0,
  input  S1,
  input  D,
  input  C,
  input  B,
  input  A,
  input  LIN,
  input  Clock,
  input  Clear,
  output QA,
  output QD,
  output QC,
  output QB
);

  wire and_1_out;

  and and_1 (and_1_out, S1, S0);
  Shift_Register #(.length(4)) shift_register_1 (
    .shift(S1), .in(LIN), .clk(Clock), .load(and_1_out), .clr(Clear), .d0(D), .q0(QD), .d1(C), .q1(QC),
    .d2(B), .q2(QB), .d3(A), .q3(QA));  // open: out
endmodule

module Uklad_A (
  input  in_1,
  input  in_2,
  input  Zegar,
  input  Reset,
  input  Reset_2,
  input  Uziemienie,
  input  Uziemienie_2,
  output QD,
  output QD_2,
  output QC,
  output QC_2,
  output QB,
  output QB_2,
  output QA,
  output QA_2
);

  wire not_1_out, not_2_out;

  not not_1 (not_1_out, in_1);
  main main_1 (
    .S1(in_1), .S0(Reset), .CLK(Zegar), .CLR(not_1_out), .SL___LIN(QA_2), .A(Uziemienie), .B(Uziemienie),
    .C(Uziemienie), .D(in_1), .QA(QA_2), .QB(QB), .QC(QC), .QD(QD));  // open: SR___RIN
  not not_2 (not_2_out, in_2);
  Uproszczony uproszczony_1 (
    .S0(Reset_2), .S1(in_2), .Clock(Zegar), .Clear(not_2_out), .QD(QD_2), .A(Uziemienie_2), .LIN(QA),
    .D(in_2), .C(Uziemienie_2), .B(Uziemienie_2), .QC(QC_2), .QB(QB_2), .QA(QA));

  // Notes on the sheet:
  //   wartość wejścia RIN bez znaczenia
endmodule

module Uklad_B (
  input  in_1,
  input  in_2,
  input  Zegar,
  input  Uziemienie,
  input  Uziemienie_2,
  output QD,
  output QD_2,
  output QC,
  output QC_2,
  output QB,
  output QB_2,
  output QA,
  output QA_2
);

  wire nand_1_out, nand_2_out, not_1_out, not_2_out;

  not not_1 (not_1_out, in_1);
  main main_1 (
    .S1(in_1), .S0(Uziemienie), .CLK(Zegar), .CLR(not_1_out), .SL___LIN(nand_1_out), .QA(QA_2), .QB(QB),
    .QC(QC), .QD(QD));  // open: SR___RIN, A, B, C, D
  nand nand_1 (nand_1_out, QD, QC, QB);
  Uproszczony uproszczony_1 (
    .S0(Uziemienie_2), .S1(in_2), .Clock(Zegar), .Clear(not_2_out), .QD(QD_2), .LIN(nand_2_out), .QC(QC_2),
    .QB(QB_2), .QA(QA));  // open: A, D, C, B
  not not_2 (not_2_out, in_2);
  nand nand_2 (nand_2_out, QD_2, QC_2, QB_2);

  // Notes on the sheet:
  //   wartość wejścia RIN i wejść równoległych bez znaczenia
endmodule

module Uklad_C (
  input  in_1,
  input  in_2,
  input  Zegar,
  input  Uziemienie,
  input  Uziemienie_2,
  output QD,
  output QD_2,
  output QC,
  output QC_2,
  output QB,
  output QB_2,
  output QA,
  output QA_2
);

  wire not_1_out, not_2_out, not_3_out, not_4_out;

  // NOT_Gate not_1 has open pins: in=open, out=not_1_out
  main main_1 (
    .S1(in_1), .S0(Uziemienie), .CLK(Zegar), .CLR(not_1_out), .SL___LIN(not_2_out), .QA(QA_2), .QB(QB),
    .QC(QC), .QD(QD));  // open: SR___RIN, A, B, C, D
  not not_2 (not_2_out, QA_2);
  Uproszczony uproszczony_1 (
    .S0(Uziemienie_2), .S1(in_2), .Clock(Zegar), .Clear(not_3_out), .QD(QD_2), .LIN(not_4_out), .QC(QC_2),
    .QB(QB_2), .QA(QA));  // open: A, D, C, B
  // NOT_Gate not_3 has open pins: in=open, out=not_3_out
  not not_4 (not_4_out, QA);

  // Notes on the sheet:
  //   wartość wejścia RIN i wejść równoległych bez znaczenia
endmodule

module test (
  input  A,
  input  A_2,
  input  Load,
  input  A_3,
  input  A_4,
  input  Shift,
  input  Input,
  input  Clock,
  input  Clear,
  output out_10,
  output out_11,
  output out_12,
  output out_13,
  output out_14
);

  Shift_Register #(.length(4)) shift_register_1 (
    .shift(Shift), .in(Input), .clk(Clock), .out(out_10), .load(Load), .clr(Clear), .d0(A), .q0(out_14),
    .d1(A_2), .q1(out_13), .d2(A_3), .q2(out_12), .d3(A_4), .q3(out_11));
endmodule
