// Logisim project 74194-niedziala.circ as structural Verilog: 1 circuit, main circuit main
module main (
  input  B,
  input  C,
  input  D,
  input  A,
  input  S1,
  input  S0,
  input  SL___LIN,
  input  SR___RIN,
  input  CLK,
  input  CLR,
  output QA,
  output QB,
  output QC,
  output QD
);

  wire and_1_out, and_2_out, and_3_out, and_4_out, and_5_out, and_6_out, and_7_out, and_8_out, and_9_out,
       and_10_out, and_11_out, and_12_out, and_13_out, and_14_out, and_15_out, and_16_out, nor_1_out,
       nor_2_out, nor_3_out, nor_4_out, not_1_out, not_2_out, not_3_out, not_4_out, not_5_out, not_6_out,
       not_7_out, not_8_out;

  not not_1 (not_1_out, S1);
  not not_2 (not_2_out, S0);
  and and_1 (and_1_out, SR___RIN, not_1_out, S0);
  not not_3 (not_3_out, CLK);
  not not_4 (not_4_out, CLR);
  and and_2 (and_2_out, S0, S1, A);
  nor nor_1 (nor_1_out, and_1_out, and_2_out, and_4_out, and_3_out);
  and and_3 (and_3_out, not_2_out, not_1_out, QA);
  and and_4 (and_4_out, not_2_out, S1, QB);
  not not_5 (not_5_out, nor_1_out);
  S_R_Flip_Flop s_r_ff_1 (
    .S(not_5_out), .clk(not_3_out), .R(nor_1_out), .Q(QA), .en(not_4_out));  // open: Qn, preset, reset
  and and_5 (and_5_out, QA, not_1_out, S0);
  and and_6 (and_6_out, S0, S1, B);
  and and_7 (and_7_out, not_2_out, S1, QC);
  nor nor_2 (nor_2_out, and_5_out, and_6_out, and_7_out, and_8_out);
  not not_6 (not_6_out, nor_2_out);
  and and_8 (and_8_out, not_2_out, not_1_out, QB);
  S_R_Flip_Flop s_r_ff_2 (
    .S(not_6_out), .clk(not_3_out), .R(nor_2_out), .Q(QB), .en(not_4_out));  // open: Qn, preset, reset
  and and_9 (and_9_out, QB, not_1_out, S0);
  and and_10 (and_10_out, S0, S1, C);
  nor nor_3 (nor_3_out, and_9_out, and_10_out, and_12_out, and_11_out);
  and and_11 (and_11_out, not_2_out, not_1_out, QC);
  and and_12 (and_12_out, not_2_out, S1, QD);
  S_R_Flip_Flop s_r_ff_3 (
    .S(not_7_out), .clk(not_3_out), .R(nor_3_out), .Q(QC), .en(not_4_out));  // open: Qn, preset, reset
  not not_7 (not_7_out, nor_3_out);
  and and_13 (and_13_out, S0, S1, D);
  and and_14 (and_14_out, QC, not_1_out, S0);
  and and_15 (and_15_out, not_2_out, S1, SL___LIN);
  nor nor_4 (nor_4_out, and_14_out, and_13_out, and_15_out, and_16_out);
  not not_8 (not_8_out, nor_4_out);
  and and_16 (and_16_out, not_2_out, not_1_out, QD);
  S_R_Flip_Flop s_r_ff_4 (
    .S(not_8_out), .clk(not_3_out), .R(nor_4_out), .Q(QD), .en(not_4_out));  // open: Qn, preset, reset

  // Notes on the sheet:
  //   eduinf.waw.pl/inf/prg/010_uc/74194.php
endmodule
