// Logisim project AK projekt 2.circ as structural Verilog: 7 circuits, main circuit main
module main (
  input  a,
  input  b,
  input  c,
  output f_a_b_c
);

  // IC_74151 ic_74151_1: pin names not known; wires that end beside it: 1'b0, 1'b1, 1'b0, 1'b0, 1'b0, 1'b0, 1'b1, 1'b0, c, b, 1'b0, a, f_a_b_c
endmodule

module \układ_1_NAND___AND_OR  (
  input  a,
  input  b,
  input  d,
  input  c,
  input  a_2,
  input  b_2,
  input  d_2,
  input  c_2,
  output f_a_b_c_d,
  output out_10
);

  wire n_c_d_out, na_nb_nc_out, nand_1_out, nand_2_out, nand_3_out, nand_4_out, nand_5_out, nand_6_out,
       nand_7_out, not_1_out, not_2_out, not_3_out;

  not not_1 (not_1_out, a);
  not not_2 (not_2_out, b);
  not not_3 (not_3_out, d);
  nand nand_1 (nand_1_out, a_2, a_2);
  nand nand_2 (nand_2_out, b_2, b_2);
  nand nand_3 (nand_3_out, d_2, d_2);
  nand nand_4 (nand_4_out, d_2, d_2);
  nand nand_5 (nand_5_out, c_2, c_2);
  and na_nb_nc (na_nb_nc_out, not_1_out, not_2_out, not_3_out);
  or or_1 (f_a_b_c_d, na_nb_nc_out, n_c_d_out);
  nor n_c_d (n_c_d_out, d, c);
  nand nand_6 (nand_6_out, nand_1_out, nand_2_out, nand_3_out);
  nand nand_7 (nand_7_out, nand_4_out, nand_5_out);
  nand nand_8 (out_10, nand_6_out, nand_7_out);

  // Notes on the sheet:
  //   podwójna negacja na końcach ominięta
  //   f(a,b,c,d) = ¬(c+d)+(¬a¬b¬c)
endmodule

module \układ_2_NAND___AND_OR  (
  input  a,
  input  b,
  input  c,
  input  a_2,
  input  b_2,
  input  c_2,
  output f_a_b_c,
  output out_8
);

  wire ab_nc_out, na_nbc_out, nand_1_out, nand_2_out, nand_3_out, nand_4_out, nand_6_out, not_1_out,
       not_2_out, not_3_out;

  nand nand_1 (nand_1_out, c_2, c_2);
  and ab_nc (ab_nc_out, a, b, not_1_out);
  not not_1 (not_1_out, c);
  not not_2 (not_2_out, a);
  not not_3 (not_3_out, b);
  and na_nbc (na_nbc_out, not_2_out, not_3_out, c);
  or or_1 (f_a_b_c, ab_nc_out, na_nbc_out);
  nand nand_2 (nand_2_out, a_2, b_2, nand_1_out);
  nand nand_3 (nand_3_out, a_2, a_2);
  nand nand_4 (nand_4_out, b_2, b_2);
  nand nand_5 (out_8, nand_2_out, nand_6_out);
  nand nand_6 (nand_6_out, nand_3_out, nand_4_out, c_2);

  // Notes on the sheet:
  //   podwójna negacja na końcach ominięta
  //   f(a,b,c) = ab¬c +¬a¬bc
endmodule

module \układ_1_MUX  (
  input  a,
  input  b,
  input  c,
  input  d,
  output f_a_b_c
);

  wire not_1_out;

  not not_1 (not_1_out, d);
  // IC_74151 ic_74151_1: pin names not known; wires that end beside it: not_1_out, not_1_out, not_1_out, 1'b0, not_1_out, 1'b0, not_1_out, 1'b0, c, b, 1'b0, a, f_a_b_c
endmodule

module \układ_2_MUX  (
  input  a,
  input  b,
  input  c,
  output f_a_b_c
);

  // IC_74151 ic_74151_1: pin names not known; wires that end beside it: 1'b0, 1'b1, 1'b0, 1'b0, 1'b0, 1'b0, 1'b1, 1'b0, c, b, 1'b0, a, f_a_b_c
endmodule

module \układ_1_symulacja  (
  output NAND_MUX
);

  wire clock_1_out, ic_74151_1_p13, ic_74161_1_p6, ic_74161_1_p7, ic_74161_1_p8, ic_74161_1_p9, nand_1_out,
       nand_2_out, nand_3_out, nand_4_out, nand_5_out, nand_6_out, nand_7_out, nand_8_out, not_1_out;

  Clock clock_1 (.out(clock_1_out));
  // IC_74161 ic_74161_1: pin names not known; wires that end beside it: clock_1_out, 1'b1, 1'b1, 1'b1, 1'b1, ic_74161_1_p6, ic_74161_1_p7, ic_74161_1_p8, ic_74161_1_p9
  not not_1 (not_1_out, ic_74161_1_p6);
  // IC_74151 ic_74151_1: pin names not known; wires that end beside it: not_1_out, not_1_out, not_1_out, 1'b0, not_1_out, 1'b0, not_1_out, 1'b0, ic_74161_1_p7, ic_74161_1_p8, 1'b0, ic_74161_1_p9, ic_74151_1_p13
  Comparator #(.width(1)) comparator_1 (.a(nand_8_out), .b(ic_74151_1_p13), .eq(NAND_MUX));  // open: gt, lt
  nand nand_1 (nand_1_out, ic_74161_1_p9, ic_74161_1_p9);
  nand nand_2 (nand_2_out, ic_74161_1_p8, ic_74161_1_p8);
  nand nand_3 (nand_3_out, ic_74161_1_p6, ic_74161_1_p6);
  nand nand_4 (nand_4_out, ic_74161_1_p6, ic_74161_1_p6);
  nand nand_5 (nand_5_out, ic_74161_1_p7, ic_74161_1_p7);
  nand nand_6 (nand_6_out, nand_1_out, nand_2_out, nand_3_out);
  nand nand_7 (nand_7_out, nand_4_out, nand_5_out);
  nand nand_8 (nand_8_out, nand_6_out, nand_7_out);

  // Notes on the sheet:
  //   d
  //   c
  //   b
  //   a
endmodule

module \układ_2_symulacja  (
  output NAND_MUX
);

  wire clock_1_out, ic_74151_1_p13, ic_74161_1_p6, ic_74161_1_p7, ic_74161_1_p8, nand_1_out, nand_2_out,
       nand_3_out, nand_4_out, nand_5_out, nand_6_out;

  Clock clock_1 (.out(clock_1_out));
  // IC_74161 ic_74161_1: pin names not known; wires that end beside it: clock_1_out, 1'b1, 1'b1, 1'b1, 1'b1, ic_74161_1_p6, ic_74161_1_p7, ic_74161_1_p8
  // IC_74151 ic_74151_1: pin names not known; wires that end beside it: 1'b0, 1'b1, 1'b0, 1'b0, 1'b0, 1'b0, 1'b1, 1'b0, ic_74161_1_p6, ic_74161_1_p7, 1'b0, ic_74161_1_p8, ic_74151_1_p13
  nand nand_1 (nand_1_out, ic_74161_1_p6, ic_74161_1_p6);
  Comparator #(.width(1)) comparator_1 (.a(ic_74151_1_p13), .b(nand_5_out), .eq(NAND_MUX));  // open: gt, lt
  nand nand_2 (nand_2_out, ic_74161_1_p8, ic_74161_1_p7, nand_1_out);
  nand nand_3 (nand_3_out, ic_74161_1_p8, ic_74161_1_p8);
  nand nand_4 (nand_4_out, ic_74161_1_p7, ic_74161_1_p7);
  nand nand_5 (nand_5_out, nand_2_out, nand_6_out);
  nand nand_6 (nand_6_out, nand_3_out, nand_4_out, ic_74161_1_p6);

  // Notes on the sheet:
  //   c
  //   b
  //   a
endmodule
