// Logisim project zadanie-inClass-7400.circ as structural Verilog: 1 circuit, main circuit main
module main (
  input  in_1,
  input  in_2,
  input  in_3,
  input  in_4,
  input  in_5,
  input  in_6,
  input  in_7,
  input  in_8,
  input  in_9,
  input  in_10,
  output out_11,
  output out_12,
  output out_13,
  output out_14
);

  wire and_2_out, d_ff_1_q, d_ff_1_qn, d_ff_2_q, d_ff_2_qn, d_ff_3_qn, dip_7400_1_p3, dip_7400_1_p6,
       dip_7400_1_p9, dip_7400_1_p12, dip_7400_2_p3, dip_7400_2_p6, dip_7400_2_p9, dip_7400_2_p12,
       dip_7400_3_p2, dip_7400_3_p7, dip_7400_3_p8, nand_1_out, nand_2_out, nand_3_out, nand_4_out,
       nand_5_out, nand_6_out, nand_7_out, nand_8_out, nand_9_out, not_1_out, not_2_out;

  // DIP_7400 dip_7400_1: pin names not known; wires that end beside it: in_6, in_6, dip_7400_1_p3, in_7, in_7, dip_7400_1_p6, dip_7400_1_p3, dip_7400_1_p6, dip_7400_1_p9, dip_7400_1_p9, dip_7400_1_p9, dip_7400_1_p12, in_9, in_10
  nand nand_1 (nand_1_out, in_2, in_2);
  nand nand_2 (nand_2_out, in_3, in_3);
  // DIP_7400 dip_7400_2: pin names not known; wires that end beside it: in_5, in_6, dip_7400_2_p3, in_6, in_7, dip_7400_2_p6, dip_7400_2_p3, dip_7400_2_p6, dip_7400_2_p9, dip_7400_2_p9, dip_7400_2_p9, dip_7400_2_p12
  not not_1 (not_1_out, in_9);
  not not_2 (not_2_out, in_10);
  nand nand_3 (nand_3_out, in_1, in_2);
  nand nand_4 (nand_4_out, in_2, in_3);
  nand nand_5 (nand_5_out, nand_1_out, nand_2_out);
  // DIP_7400 dip_7400_3: pin names not known; wires that end beside it: dip_7400_2_p12, dip_7400_3_p2, out_13, dip_7400_1_p12, in_5, dip_7400_3_p2, dip_7400_3_p7, dip_7400_3_p8
  buf and_1 (dip_7400_3_p7, in_8);  // AND_Gate
  buf and_2 (and_2_out, in_9);  // AND_Gate
  and and_3 (dip_7400_3_p8, in_8, not_1_out, not_2_out);
  nand nand_6 (nand_6_out, nand_3_out, nand_4_out);
  nand nand_7 (nand_7_out, nand_5_out, nand_5_out);
  or or_1 (out_14, dip_7400_3_p7, and_2_out, dip_7400_3_p8);
  nand nand_8 (nand_8_out, nand_6_out, nand_6_out);
  nand nand_9 (nand_9_out, nand_7_out, in_1);
  nand nand_10 (out_11, nand_8_out, nand_9_out);
  D_Flip_Flop #(.trigger("falling")) d_ff_1 (
    .clk(in_4), .D(d_ff_1_qn), .Q(d_ff_1_q), .Qn(d_ff_1_qn));  // open: preset, en, reset
  D_Flip_Flop #(.trigger("falling")) d_ff_2 (
    .clk(d_ff_1_q), .D(d_ff_2_qn), .Q(d_ff_2_q), .Qn(d_ff_2_qn));  // open: preset, en, reset
  D_Flip_Flop #(.trigger("falling")) d_ff_3 (
    .clk(d_ff_2_q), .D(d_ff_3_qn), .Q(out_12), .Qn(d_ff_3_qn));  // open: preset, en, reset

  // Notes on the sheet:
  //   wersja "domyślna"
  //   wersja tylko nand
  //   wersja tylko 7400
  //   licznik zrobiony z przerzutników D
  //   https://github.com/r0the/logi7400 link do 7400
endmodule
